// Logisim project blinkomat.circ as structural Verilog: 1 circuit, main circuit main
module main (
  input  [7:0] in_1
);

  wire and_1_out, and_2_out, and_3_out, and_4_out, and_5_out, clock_1_out, comparator_1_eq, comparator_2_eq,
       not_1_out, not_2_out, or_1_out, or_2_out, or_4_out, or_5_out, pull_resistor_1_node,
       pull_resistor_2_node, pull_resistor_3_node, pull_resistor_4_node, pull_resistor_6_node,
       pull_resistor_7_node, reset_out;
  wire [7:0] counter_1_q, counter_2_q, counter_3_q, or_3_out, register_1_q, register_2_q, rom_1_data;

  Pull_Resistor pull_resistor_1 (.node(pull_resistor_1_node));
  Pull_Resistor #(.pull(1)) pull_resistor_2 (.node(pull_resistor_2_node));
  Clock clock_1 (.out(clock_1_out));
  Hex_Digit_Display hex_digit_display_1 (.value(counter_1_q[7:4]));  // open: dp
  Counter counter_1 (
    .load(pull_resistor_1_node), .count(pull_resistor_2_node), .Q(counter_1_q), .clk(clock_1_out),
    .clr(or_1_out));  // open: D, carry
  or or_1 (or_1_out, comparator_1_eq, reset_out);
  Hex_Digit_Display hex_digit_display_2 (.value(counter_1_q[3:0]));  // open: dp
  Comparator comparator_1 (.a(counter_1_q), .b(in_1), .eq(comparator_1_eq));  // open: gt, lt
  Hex_Digit_Display hex_digit_display_3 (.value(in_1[7:4]));  // open: dp
  Hex_Digit_Display hex_digit_display_4 (.value(in_1[3:0]));  // open: dp
  and and_1 (and_1_out, rom_1_data[7], ~rom_1_data[6]);  // AND_Gate
  and and_2 (and_2_out, rom_1_data[7], rom_1_data[6]);
  Register register_1 (.D(rom_1_data), .en(and_2_out), .Q(register_1_q), .clk(or_4_out), .clr(reset_out));
  Button reset (.out(reset_out));
  Pull_Resistor pull_resistor_3 (.node(pull_resistor_3_node));
  Counter counter_2 (
    .load(pull_resistor_3_node), .count(pull_resistor_4_node), .Q(counter_2_q), .clk(comparator_1_eq),
    .clr(or_2_out));  // open: D, carry
  Pull_Resistor #(.pull(1)) pull_resistor_4 (.node(pull_resistor_4_node));
  or or_2 (or_2_out, rom_1_data[7], reset_out, comparator_2_eq);
  Pull_Resistor pull_resistor_5 (.node(or_3_out[7]));
  Comparator comparator_2 (
    .a(counter_2_q), .b({{2{or_3_out[7]}}, register_1_q[5:1], or_3_out[0]}), .eq(comparator_2_eq));  // open: gt, lt
  ROM rom_1 (.addr(counter_3_q), .data(rom_1_data));  // open: sel
  or or_3 (or_3_out[0], register_1_q[0], and_3_out);
  and and_3 (and_3_out, ~register_1_q[5], ~register_1_q[4], ~register_1_q[3], ~register_1_q[2], ~register_1_q[1]);  // AND_Gate
  and and_4 (and_4_out, ~and_2_out, comparator_2_eq);  // AND_Gate
  or or_4 (or_4_out, and_4_out, and_5_out);
  and and_5 (and_5_out, and_2_out, clock_1_out);
  Pull_Resistor pull_resistor_6 (.node(pull_resistor_6_node));
  Pull_Resistor #(.pull(1)) pull_resistor_7 (.node(pull_resistor_7_node));
  Register register_2 (.D(rom_1_data), .en(not_1_out), .Q(register_2_q), .clk(not_2_out), .clr(reset_out));
  not not_1 (not_1_out, rom_1_data[7]);
  not not_2 (not_2_out, clock_1_out);
  Counter counter_3 (
    .load(pull_resistor_6_node), .count(pull_resistor_7_node), .Q(counter_3_q), .clk(or_4_out), .clr(or_5_out));  // open: D, carry
  or or_5 (or_5_out, and_1_out, reset_out);
  LED led_1 (.in(register_2_q[5]));
  Hex_Digit_Display hex_digit_display_5 (.value({{2{or_3_out[7]}}, register_1_q[5:4]}));  // open: dp
  Hex_Digit_Display hex_digit_display_6 (.value(counter_2_q[7:4]));  // open: dp
  LED led_2 (.in(register_2_q[3]));
  LED led_3 (.in(register_2_q[2]));
  LED led_4 (.in(register_2_q[4]));
  Hex_Digit_Display hex_digit_display_7 (.value({register_1_q[3:1], or_3_out[0]}));  // open: dp
  Hex_Digit_Display hex_digit_display_8 (.value(counter_2_q[3:0]));  // open: dp
  LED led_5 (.in(register_2_q[0]));
  LED led_6 (.in(register_2_q[1]));

  // Notes on the sheet:
  //   base clock
  //   set period
  //   cycle length
  //   loop
  //   contents of rom_1 (hex, n*v repeats v):
  //   cf 1 2 4 8 10 20 1 2 4 8 10 20 1 2 4 8 10 20 1 2 4 8 10 20 c1 1 2 4 8 10 20 1 2 4 8 10 20 1 2 4 8 10
  //   20 1 2 4 8 10 20 cf 0 c1 3f 0 3f 0 3f 0 3f cf 0 c2 3f 0 3f 0 3f 0 3f cf 0 c4 3f 0 3f 0 3f 0 3f cf 0
  //   c8 3f 0 3f 0 3f 0 3f cf 0 d0 3f 0 3f 0 3f 0 3f cf 0 e0 3f 0 3f 0 3f 0 3f cf 0 c1 15 26 15 26 15 26
  //   15 26 cf 0 80
  //   period
  //   blink clock
endmodule
