// Logisim project blinkomat2.circ as structural Verilog: 1 circuit, main circuit main
module main (
);

  wire and_1_out, and_2_out, and_3_out, and_4_out, and_5_out, clock_1_out, comparator_1_eq, not_1_out,
       not_2_out, or_1_out, or_3_out, or_4_out, pull_resistor_1_node, pull_resistor_2_node,
       pull_resistor_4_node, pull_resistor_5_node, reset_out;
  wire [7:0] counter_1_q, counter_2_q, or_2_out, register_1_q, register_2_q, rom_1_data;

  Clock clock_1 (.out(clock_1_out));
  and and_1 (and_1_out, rom_1_data[7], ~rom_1_data[6]);  // AND_Gate
  and and_2 (and_2_out, rom_1_data[7], rom_1_data[6]);
  Register register_1 (.D(rom_1_data), .en(and_2_out), .Q(register_1_q), .clk(or_3_out), .clr(reset_out));
  Pull_Resistor pull_resistor_1 (.node(pull_resistor_1_node));
  Counter counter_1 (
    .load(pull_resistor_1_node), .count(pull_resistor_2_node), .Q(counter_1_q), .clk(clock_1_out),
    .clr(or_1_out));  // open: D, carry
  Pull_Resistor #(.pull(1)) pull_resistor_2 (.node(pull_resistor_2_node));
  or or_1 (or_1_out, rom_1_data[7], reset_out, comparator_1_eq);
  Pull_Resistor pull_resistor_3 (.node(or_2_out[7]));
  Comparator comparator_1 (
    .a(counter_1_q), .b({{2{or_2_out[7]}}, register_1_q[5:1], or_2_out[0]}), .eq(comparator_1_eq));  // open: gt, lt
  ROM rom_1 (.addr(counter_2_q), .data(rom_1_data));  // open: sel
  or or_2 (or_2_out[0], register_1_q[0], and_3_out);
  and and_3 (and_3_out, ~register_1_q[5], ~register_1_q[4], ~register_1_q[3], ~register_1_q[2], ~register_1_q[1]);  // AND_Gate
  and and_4 (and_4_out, ~and_2_out, comparator_1_eq);  // AND_Gate
  or or_3 (or_3_out, and_4_out, and_5_out);
  and and_5 (and_5_out, and_2_out, clock_1_out);
  Pull_Resistor pull_resistor_4 (.node(pull_resistor_4_node));
  Pull_Resistor #(.pull(1)) pull_resistor_5 (.node(pull_resistor_5_node));
  Register register_2 (.D(rom_1_data), .en(not_1_out), .Q(register_2_q), .clk(not_2_out), .clr(reset_out));
  not not_1 (not_1_out, rom_1_data[7]);
  not not_2 (not_2_out, clock_1_out);
  Counter counter_2 (
    .load(pull_resistor_4_node), .count(pull_resistor_5_node), .Q(counter_2_q), .clk(or_3_out), .clr(or_4_out));  // open: D, carry
  or or_4 (or_4_out, and_1_out, reset_out);
  LED led_1 (.in(register_2_q[6]));
  Button reset (.out(reset_out));
  Hex_Digit_Display hex_digit_display_1 (.value({{2{or_2_out[7]}}, register_1_q[5:4]}));  // open: dp
  Hex_Digit_Display hex_digit_display_2 (.value(counter_1_q[7:4]));  // open: dp
  LED led_2 (.in(register_2_q[5]));
  LED led_3 (.in(register_2_q[3]));
  LED led_4 (.in(register_2_q[4]));
  Hex_Digit_Display hex_digit_display_3 (.value({register_1_q[3:1], or_2_out[0]}));  // open: dp
  Hex_Digit_Display hex_digit_display_4 (.value(counter_1_q[3:0]));  // open: dp
  LED led_5 (.in(register_2_q[2]));
  LED led_6 (.in(register_2_q[1]));
  LED led_7 (.in(register_2_q[0]));

  // Notes on the sheet:
  //   set period
  //   system clock (ca 10Hz?)
  //   period
  //   register
  //   blink counter
  //   loop
  //   EEPROM (flash)
  //   contents of rom_1 (hex, n*v repeats v):
  //   cf 1 2 4 8 10 20 40 1 2 4 8 10 20 40 ff f 70 f 70 d0 70 f 70 f c8 f 70 f 70 c4 70 f 0 1 2 1 0 1 2 1
  //   0 3 0 3 0 1 2 1 0 f 7 e 7 f 0 c8 55 2c 55 2c 0 0 7f 0 0 7f 0 0 55 2c 55 2c 0 0 7f 0 0 1 2 4 9 12 24
  //   49 12 24 49 12 24 49 24 48 10 20 40 4*0 41 63 77 7f 3e 1c 4*8 0 8 8 8 0 8 8 0 8 0 0 8 4*0 c1 7f 0 7f
  //   0 7f 0 7f 0 7f 0 7f 0 7f 0 7f 0 7f ff 0 80
  //   clock mixer
  //   address
  //   output register
  //   2
  //   (4 bits are one nibble)
  //   0000 : 0
  //   0001 : 1
  //   0010 : 2
  //   0011 : 3
  //   0100 : 4
  //   0101 : 5
  //   0110 : 6
  //   0111 : 7
  //   nibble 1
  //   3
  //   1
  //   0
  //   period
  //   blink clock
  //   binary to hexadecimal
  //   1000 : 8
  //   1001 : 9
  //   1010 : a
  //   1011 : b
  //   1100 : c
  //   1101 : d
  //   1110 : e
  //   1111 : f
  //   nibble 0
  //   1
  //   2
  //   0
endmodule
